# Fritzing sketch YouTwoFritz1 (saved by Fritzing 0.9.4)
breadboards: 3

parts:
  Breadboard4 = Breadboard Split Power
  Breadboard5 = Breadboard Split Power
  Part1 = 12 NeoPixel Ring [part_number=1643]
  RG_encoder1 = SprkFn RG Encoder [package="DIP (Dual Inline) [THT]"]
  Argon2 = Particle Argon
  DotStar1 = DorStar LED Strip [part_number=2239]

nets:
  GND: Breadboard4.pin3Z, Breadboard4.pin20Z, Breadboard4.pin29Z, Breadboard5.pin3Z, Breadboard5.pin11Z, Breadboard5.pin28Z, Part1.GND, Argon2.GND, DotStar1.GND
  VDD: Breadboard4.pin4Y, Breadboard4.pin15Y, Breadboard4.pin17Y, Breadboard4.pin21Y, Breadboard4.pin29Y, Breadboard5.pin3Y, Breadboard5.pin15Y, Breadboard5.pin17Y, Breadboard5.pin29Y, Part1.VDD, Argon2.3.3V, DotStar1.+5V
  N1: Part1.IN, Argon2.A3
  N2: RG_encoder1.A, Argon2.A5
  N3: RG_encoder1.B, Argon2.A4
  N4: Argon2.SCK, DotStar1.CI
  N5: Argon2.MO, DotStar1.DI

custom parts:
  Breadboard Split Power: A custom 6 pin per group power supply strip where the top row (ground) is all bussed together and the bottom row (+V) is split in two groups of 12 pins. This version is modified to be a loadable part and was rescaled to be on the standard 1px = 1thou grid with the size set in inches
  12 NeoPixel Ring: 12 ultra bright smart LED NeoPixels are arranged in a circle with 1.5" (37mm) outer diameter. The rings are 'chainable' - connect the output pin of one to the input pin of another. Use only one microcontroller pin to control as many as you can chain together! Each LED is addressable as the driver chip is inside the LED. Each one has ~18mA constant current drive so the color will be very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
  SprkFn RG Encoder: SparkFun RG Rotary Encoder
  Particle Argon: The Argon is a powerful Wi-Fi enabled development board that can act as either a standalone Wi-Fi endpoint or Wi-Fi enabled gateway for Particle Mesh networks. It is based on the Nordic nRF52840 and has built-in battery charging circuitry so it’s easy to connect a Li-Po and deploy your local network in minutes. The Argon is great for connecting existing projects to the Particle Device Cloud or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
  DorStar LED Strip: DotStar LED strip, black, 60 LEDs/m
